# Fritzing sketch ElectricityMeter_with_DS1307 (saved by Fritzing 0.9.3b)
breadboards: 1

parts:
  Part1 = Real Time Clock Module - DS1307 RTC Breakout Board
  Part2 = Arduino Uno (Rev3)
  J1 = Screw terminal - 2 pins [package=THT]
  J2 = Screw terminal - 2 pins [package=THT]
  R1 = Resistor [tolerance=±5% resistance=10k package=THT]
  R2 = Resistor [tolerance=±5% resistance=10k package=THT]
  R3 = Resistor [tolerance=±5% resistance=220 package=THT]
  LED1 = LED - 5mm [color="Red (633nm)" package="5 mm [THT]"]

nets:
  5V: Part1.5V, Part2.5V, J1.pin1, J2.pin1
  GND: Part1.GND, Part2.GND, R1.Pin_0, R2.Pin_0, R3.Pin_0
  N1: Part1.SCL, Part2.A5/SCL
  N2: Part1.SDA, Part2.A4/SDA
  N3: Part2.D9_PWM, LED1.anode
  N4: Part2.D2, J1.pin2, R1.Pin_1
  N5: Part2.D3_PWM, J2.pin2, R2.Pin_1
  N6: R3.Pin_1, LED1.cathode
